# Fritzing sketch sketch (saved by Fritzing 0.8.4b)
circuit board: 11.664cm x 10.2263cm
breadboards: 1

parts:
  leftEyeRed = LED - 5mm [color="Red (635nm)" package="5 mm [THT]"]
  rightEyeRed = LED - 5mm [color="Red (635nm)" package="5 mm [THT]"]
  Head = Basic Servo
  rightEyeBlue = LED - 5mm [color="Blue (505nm)" package="5 mm [THT]"]
  leftEyeBlue = LED - 5mm [color="Blue (505nm)" package="5 mm [THT]"]
  Buzzer = Piezo Speaker
  UNO = Arduino Uno (Rev3)
  Turnplate = Basic Servo
  元件1 = TCS3200 Color Sensor

nets:
  GND: leftEyeRed.cathode, rightEyeRed.cathode, Head.gnd, rightEyeBlue.cathode, leftEyeBlue.cathode, Buzzer.pin1, UNO.GND, Turnplate.gnd, 元件1.GND#13
  N1: leftEyeRed.anode, rightEyeRed.anode, UNO.D7
  VCC: Head.vcc, UNO.5V, Turnplate.vcc, 元件1.VDD
  N2: Head.pulse, UNO.D6_PWM
  N3: rightEyeBlue.anode, leftEyeBlue.anode, UNO.D4
  N4: Buzzer.pin2, UNO.D3_PWM
  N5: UNO.D8, 元件1.GND#16, 元件1.S0
  N6: UNO.D9_PWM, 元件1.S1
  N7: UNO.D10_PWM/SS, 元件1.S2
  N8: UNO.D11_PWM/MOSI, 元件1.S3
  N9: UNO.D2, 元件1.OUT
  N10: UNO.D5_PWM, Turnplate.pulse

custom parts:
  TCS3200 Color Sensor: TCS3200 Color Sensor by DF Robot
